# Fritzing sketch mainboard (saved by Fritzing 0.9.3b)
circuit board: 3cm x 6.5cm
circuit board: 7.80366cm x 6.58223cm
breadboards: 1

parts:
  Q2 = PNP-Transistor [package="TO92 [THT]"]
  Q3 = NPN-Transistor [package="TO92 [THT]"]
  Q4 = NPN-Transistor [package="TO92 [THT]"]
  R1 = Resistor [tolerance=±5% resistance=10k package=THT]
  R3 = Resistor [tolerance=±5% resistance=10k package=THT]
  R4 = Resistor [tolerance=±5% resistance=10k package=THT]
  R2 = Resistor [tolerance=±5% resistance=10k package=THT]
  J1 = female pin header, 2 pins [form="♀ (female)"]
  Q5 = PNP-Transistor [package="TO92 [THT]"]
  Q6 = PNP-Transistor [package="TO92 [THT]"]
  Q7 = NPN-Transistor [package="TO92 [THT]"]
  Q8 = NPN-Transistor [package="TO92 [THT]"]
  R8 = Resistor [tolerance=±5% resistance=10k package=THT]
  R6 = Resistor [tolerance=±5% resistance=10k package=THT]
  R7 = Resistor [tolerance=±5% resistance=10k package=THT]
  R5 = Resistor [tolerance=±5% resistance=10k package=THT]
  J2 = female pin header, 2 pins [form="♀ (female)"]
  Shutdown = Pushbutton [package="[THT]"]
  MinUMU9v5 = mystery part, 5 pins [chip_label=?]
  POWER = USB Connectors [package=usb-minib-nostop]  # not connected
  USB = USB Connectors [package=usb-minib-nostop]  # not connected
  HDMI = USB+SHIELD [package=usb-b-pth]  # not connected
  J3 = female pin header, 3 pins [form="♀ (female)"]
  J4 = female pin header, 3 pins [form="♀ (female)"]
  D1 = male pin header, 2 pins [form="♂ (male)"]
  Q1 = PNP-Transistor [package="TO92 [THT]"]
  D3 = male pin header, 2 pins [form="♂ (male)"]
  D2 = male pin header, 2 pins [form="♂ (male)"]
  D4 = male pin header, 2 pins [form="♂ (male)"]
  D7 = male pin header, 2 pins [form="♂ (male)"]
  D5 = male pin header, 2 pins [form="♂ (male)"]
  D8 = male pin header, 2 pins [form="♂ (male)"]
  D9 = male pin header, 2 pins [form="♂ (male)"]
  HC-SR04 = hc-sr04
  R9 = Resistor [tolerance=±5% resistance=1k package=THT]
  R10 = Resistor [tolerance=±5% resistance=2.2k package=THT]
  GPIO = Generic double row male header - 40 pins [form="♂ (male)" package=THT]
  5v = female pin header, 2 pins [form="♀ (female)"]
  10v = female pin header, 2 pins [form="♀ (female)"]
  C2 = Ceramic Capacitor [capacitance=100nF package="100 mil [THT, multilayer]"]
  C1 = Electrolytic Capacitor [capacitance=1µF package="100 mil [THT, electrolytic]"]
  C3 = Ceramic Capacitor [capacitance=100nF package="100 mil [THT, multilayer]"]
  R11 = Resistor [tolerance=±5% resistance=1k package=THT]
  R12 = Resistor [tolerance=±5% resistance=2.2k package=THT]
  ATmega328 = atmega328 [package=dip]
  XTAL = CRYSTAL - kHz [frequency="16 MHz"]
  C4 = Ceramic Capacitor [capacitance=22pF package="100 mil [THT, multilayer]"]
  C5 = Ceramic Capacitor [capacitance=22pF package="100 mil [THT, multilayer]"]
  R13 = Resistor [tolerance=±5% resistance=2.2k package=THT]

nets:
  N1: Q2.E, Q5.E, Q6.E, D1.pin1, Q1.E, D2.pin1, D5.pin1, D8.pin1, 10v.pin1, R11.Pin_1
  N2: Q2.B, R2.Pin_0
  N3: Q2.C, Q4.C, J1.pin1, D2.pin2, D4.pin1
  GND: Q3.E, Q4.E, Q7.E, Q8.E, Shutdown.Pin_1, Shutdown.Pin_2, Shutdown.Pin_3, Shutdown.Pin_4, J3.pin2, J4.pin2, D3.pin2, D4.pin2, D7.pin2, D9.pin2, HC-SR04.GND, GPIO.pin39, GPIO.pin38, GPIO.pin30, GPIO.pin6, 5v.pin2, 10v.pin2, C2.1, C1.-, C3.1, R12.Pin_0, ATmega328.GND, C4.1, C5.1
  N4: Q3.B, R3.Pin_1
  N5: Q3.C, J1.pin2, D1.pin2, Q1.C, D3.pin1
  N6: Q4.B, R4.Pin_1
  N7: R1.Pin_0, Q1.B
  N8: R1.Pin_1, R3.Pin_0, ATmega328.D6_(PWM)
  N9: R4.Pin_0, R2.Pin_1, ATmega328.D5_(PWM)
  N10: Q5.B, R5.Pin_0
  N11: Q5.C, Q7.C, J2.pin2, D7.pin1, D5.pin2
  N12: Q6.B, R6.Pin_0
  N13: Q6.C, Q8.C, J2.pin1, D8.pin2, D9.pin1
  N14: Q7.B, R7.Pin_1
  N15: Q8.B, R8.Pin_1
  N16: R8.Pin_0, R6.Pin_1, ATmega328.D10_(PWM)
  N17: R7.Pin_0, R5.Pin_1, ATmega328.D9_(PWM)
  N18: MinUMU9v5.pin1, GPIO.pin5, ATmega328.A5
  N19: MinUMU9v5.pin2, GPIO.pin3, ATmega328.A4
  N20: MinUMU9v5.pin3, GPIO.pin14
  N21: MinUMU9v5.pin5, GPIO.pin17
  N22: J3.pin1, ATmega328.D2
  VCC: J3.pin3, J4.pin3, HC-SR04.VCC, GPIO.pin4, 5v.pin1, C2.0, C1.+, C3.0, ATmega328.VCC, ATmega328.AVCC, ATmega328.AREF, R13.Pin_0
  N23: J4.pin1, ATmega328.D3_(PWM)
  N24: HC-SR04.Trig, GPIO.pin22
  N25: HC-SR04.Echo, R9.Pin_0
  N26: R9.Pin_1, R10.Pin_1, GPIO.pin18
  N27: R10.Pin_0, GPIO.pin20
  N28: R11.Pin_0, R12.Pin_1, ATmega328.A3
  N29: ATmega328.RESET, R13.Pin_1
  N30: ATmega328.XLAT1, XTAL.pin_0, C4.0
  N31: ATmega328.XLAT2, XTAL.pin_1, C5.0

custom parts:
  Generic double row male header - 40 pins: Generic double row male header
